# Fritzing sketch fermentcontrol (saved by Fritzing 0.9.0b)
circuit board: 6.23395cm x 3.94028cm
breadboards: 1

parts:
  R1 = Resistor [tolerance=±5% resistance=100k package=THT]
  U1 = GAS_SENSOR [package=mq-3]
  Bauteil1 = Arduino Uno (Rev3)
  DS1 = DS18B20 1-Wire Temperature Sensor [part_number=DS18B20]
  R2 = Resistor [tolerance=±5% resistance=4.7k package=THT]

nets:
  GND: R1.Pin_0, U1.H2, Bauteil1.GND, DS1.GND
  N1: R1.Pin_1, U1.B1, Bauteil1.A1
  5V: U1.A1, U1.H1, Bauteil1.5V, DS1.VDD, R2.Pin_1
  N2: Bauteil1.D10_PWM/SS, DS1.DQ, R2.Pin_0
