# Fritzing sketch sketch (saved by Fritzing 0.9.0b)
circuit board: 8.46667cm x 5.64444cm
breadboards: 1

parts:
  Raspberry_Pi1 = Raspberry Pi B rev2  # not connected
  Pi1 = Adafruit Pi Cobbler
  Heat_1 = Resistor [tolerance=±5% resistance=10k package=THT]
  Heat_2 = Resistor [tolerance=±5% resistance=10k package=THT]
  Q1 = NPN-Transistor [package="TO92 [THT]"]
  D2 = Rectifier Diode [part_number=1N4001 package="300 mil [THT]"]
  M1 = DC Motor
  M2 = DC Motor
  Power_plug1 = Power plug
  Q2 = NPN-Transistor [package="TO92 [THT]"]
  U1 = TEMPERATURE-SENSOR [package=to-92]

nets:
  N1: Pi1.5V0, U1.VCC
  GND: Pi1.GND, Q1.C, D2.anode, Power_plug1.GND, Q2.C, U1.GND
  N2: Pi1.#17, U1.ADJ
  N3: Pi1.#21, Q2.E
  N4: Pi1.#22, Q1.E
  N5: Heat_1.Pin_0, Heat_2.Pin_0, Q2.B
  N6: Heat_1.Pin_1, Heat_2.Pin_1, M1.pin_1, M2.pin_1, Power_plug1.VCC
  N7: Q1.B, D2.cathode, M1.pin_2, M2.pin_2

notes:
  Transistor ersetzen für Last ca. je 4 A

custom parts:
  Adafruit Pi Cobbler: Adafruit Pi Cobbler GPIO Breakout for Raspberry Pi
